# Fritzing sketch Accensione di 3 LED in diverso modo con un pulsante (Progetto 4) (saved by Fritzing 0.9.3b)
breadboards: 1

parts:
  Componente1 = Arduino Uno (Rev3)
  R1 = Resistor [tolerance=±5% resistance=1k package=THT]
  LED1 = LED - 5mm [color="Red (633nm)" package="5 mm [THT]"]
  LED2 = LED - 5mm [color="White (4500K)" package="5 mm [THT]"]
  LED3 = LED - 5mm [color="Green (555nm)" package="5 mm [THT]"]
  R2 = Resistor [tolerance=±5% resistance=1k package=THT]
  R3 = Resistor [tolerance=±5% resistance=1k package=THT]
  S1 = Pushbutton [package="[THT]"]
  R4 = Resistor [tolerance=±5% resistance=1k package=THT]

nets:
  N1: Componente1.D2, S1.Pin_1, S1.Pin_2, R4.Pin_0
  N2: Componente1.D3_PWM, LED3.cathode
  N3: Componente1.D4, LED2.cathode
  N4: Componente1.D5_PWM, LED1.cathode
  N5: Componente1.5V, R1.Pin_0, R2.Pin_1, R3.Pin_1, R4.Pin_1
  N6: Componente1.GND, S1.Pin_3, S1.Pin_4
  N7: R1.Pin_1, LED1.anode
  N8: LED2.anode, R2.Pin_0
  N9: LED3.anode, R3.Pin_0
